// Logisim project Two’s Complement _Comparator_Sharma_Akash.circ as structural Verilog: 3 circuits, main circuit main
module main (
  input  B1,
  input  B2,
  input  B3,
  input  B4,
  input  B5,
  input  A1,
  input  A2,
  input  A3,
  input  A4,
  input  A5,
  output A_B,
  output A_B_2,
  output A_B_3
);

  _5_Bit_Comparator u_5_bit_comparator_1 (
    .control(A5), .A5(A5), .A4(A4), .A3(A3), .A2(A2), .A1(A1), .control_2(B5), .B5(B5), .B4(B4), .B3(B3),
    .B2(B2), .B1(B1), .out_13(A_B_2), .out_15(A_B_3), .out_16(A_B));  // open: Carry_Over, Carry_Over_2
endmodule

module HALF_ADDER (
  input  A,
  input  B,
  output SUM,
  output CARRY
);

  xor xor_1 (SUM, A, B);
  and and_1 (CARRY, A, B);
endmodule

// Comparator
module _5_Bit_Comparator (
  input  control,
  input  A5,
  input  A4,
  input  A3,
  input  A2,
  input  A1,
  input  control_2,
  input  B5,
  input  B4,
  input  B3,
  input  B2,
  input  B1,
  output out_13,
  output Carry_Over,
  output out_15,
  output out_16,
  output Carry_Over_2
);

  wire A1_prime_B1_out, A1_prime_out, A1_XOR_B1_out, A2_prime_B2_out, A2_prime_out, A2_XOR_B2_out,
       A3_prime_B3_out, A3_prime_out, A3_XOR_B3_out, A4_prime_B4_out, A4_XOR_B4_out, A5_prime_B5_prime_out,
       A5_prime_out, A5_XOR_B5_out, AND1_out, and_1_out, and_2_out, and_3_out, and_4_out, and_5_out,
       and_6_out, and_7_out, and_9_out, and_10_out, and_11_out, B1_prime_A1_out, B2_prime_A2_out,
       B3_prime_A3_out, B4_prime_A4_out, B5_prime_A5_out, B5_prime_out, half_adder_1_carry, half_adder_1_sum,
       half_adder_2_carry, half_adder_2_sum, half_adder_3_carry, half_adder_3_sum, half_adder_4_carry,
       half_adder_4_sum, half_adder_5_sum, half_adder_6_carry, half_adder_6_sum, half_adder_7_carry,
       half_adder_7_sum, half_adder_8_carry, half_adder_8_sum, half_adder_9_carry, half_adder_9_sum,
       half_adder_10_sum, not_1_out, not_2_out, not_3_out, not_4_out, not_5_out, not_6_out, not_7_out,
       not_8_out, not_9_out, not_10_out, OR1_out, OR2_out, OR3_out, or_1_out, or_2_out, or_3_out, XOR3_out,
       XOR4_out, xor_1_out, xor_2_out, xor_3_out, xor_4_out, xor_5_out, xor_6_out, xor_7_out, xor_8_out,
       xor_9_out, xor_10_out, XOR_A4_B4_A3_B3_out;

  xor xor_1 (xor_1_out, A5, control);
  xor xor_2 (xor_2_out, A4, control);
  xor xor_3 (xor_3_out, A3, control);
  xor xor_4 (xor_4_out, A2, control);
  xor xor_5 (xor_5_out, A1, control);
  xor xor_6 (xor_6_out, B5, control_2);
  xor xor_7 (xor_7_out, B4, control_2);
  xor xor_8 (xor_8_out, B3, control_2);
  xor xor_9 (xor_9_out, B2, control_2);
  xor xor_10 (xor_10_out, B1, control_2);
  HALF_ADDER half_adder_1 (.A(control), .B(xor_1_out), .SUM(half_adder_1_sum), .CARRY(half_adder_1_carry));
  HALF_ADDER half_adder_2 (.A(half_adder_1_carry), .B(xor_2_out), .SUM(half_adder_2_sum), .CARRY(half_adder_2_carry));
  HALF_ADDER half_adder_3 (.A(half_adder_2_carry), .B(xor_3_out), .SUM(half_adder_3_sum), .CARRY(half_adder_3_carry));
  HALF_ADDER half_adder_4 (.A(half_adder_3_carry), .B(xor_4_out), .SUM(half_adder_4_sum), .CARRY(half_adder_4_carry));
  HALF_ADDER half_adder_5 (.A(half_adder_4_carry), .B(xor_5_out), .SUM(half_adder_5_sum), .CARRY(Carry_Over));
  HALF_ADDER half_adder_6 (.A(control_2), .B(xor_6_out), .SUM(half_adder_6_sum), .CARRY(half_adder_6_carry));
  HALF_ADDER half_adder_7 (.A(half_adder_6_carry), .B(xor_7_out), .SUM(half_adder_7_sum), .CARRY(half_adder_7_carry));
  HALF_ADDER half_adder_8 (.A(half_adder_7_carry), .B(xor_8_out), .SUM(half_adder_8_sum), .CARRY(half_adder_8_carry));
  HALF_ADDER half_adder_9 (.A(half_adder_8_carry), .B(xor_9_out), .SUM(half_adder_9_sum), .CARRY(half_adder_9_carry));
  HALF_ADDER half_adder_10 (.A(half_adder_9_carry), .B(xor_10_out), .SUM(half_adder_10_sum), .CARRY(Carry_Over_2));
  not B5_prime (B5_prime_out, half_adder_6_sum);
  not A5_prime (A5_prime_out, half_adder_1_sum);
  and A5_prime_B5_prime (A5_prime_B5_prime_out, half_adder_6_sum, A5_prime_out);
  not not_1 (not_1_out, half_adder_7_sum);
  and B5_prime_A5 (B5_prime_A5_out, half_adder_1_sum, B5_prime_out);
  not not_2 (not_2_out, A5_XOR_B5_out);
  xor A5_XOR_B5 (A5_XOR_B5_out, half_adder_1_sum, half_adder_6_sum);
  not A3_prime (A3_prime_out, half_adder_2_sum);
  or OR1 (OR1_out, A5_prime_B5_prime_out, AND1_out);
  or or_1 (or_1_out, B5_prime_A5_out, and_1_out);
  and and_1 (and_1_out, not_2_out, B4_prime_A4_out);
  not not_3 (not_3_out, half_adder_8_sum);
  and B4_prime_A4 (B4_prime_A4_out, not_1_out, half_adder_2_sum);
  xor A4_XOR_B4 (A4_XOR_B4_out, half_adder_2_sum, half_adder_7_sum);
  and A4_prime_B4 (A4_prime_B4_out, half_adder_7_sum, A3_prime_out);
  and and_2 (and_2_out, not_2_out, not_4_out);
  and and_3 (and_3_out, and_2_out, B3_prime_A3_out);
  and B3_prime_A3 (B3_prime_A3_out, not_3_out, half_adder_3_sum);
  not not_4 (not_4_out, A4_XOR_B4_out);
  not A2_prime (A2_prime_out, half_adder_3_sum);
  and AND1 (AND1_out, A4_prime_B4_out, not_2_out);
  or or_2 (or_2_out, or_1_out, and_3_out);
  not not_5 (not_5_out, half_adder_9_sum);
  not not_6 (not_6_out, A3_XOR_B3_out);
  xor A3_XOR_B3 (A3_XOR_B3_out, half_adder_3_sum, half_adder_8_sum);
  and XOR_A4_B4_A3_B3 (XOR_A4_B4_A3_B3_out, not_4_out, not_2_out);
  and A3_prime_B3 (A3_prime_B3_out, A2_prime_out, half_adder_8_sum);
  or OR2 (OR2_out, OR1_out, and_5_out);
  and and_4 (and_4_out, and_6_out, B2_prime_A2_out);
  and B2_prime_A2 (B2_prime_A2_out, not_5_out, half_adder_4_sum);
  xor A2_XOR_B2 (A2_XOR_B2_out, half_adder_4_sum, half_adder_9_sum);
  and and_5 (and_5_out, A3_prime_B3_out, XOR_A4_B4_A3_B3_out);
  and and_6 (and_6_out, and_2_out, not_6_out);
  or or_3 (or_3_out, or_2_out, and_4_out);
  not not_7 (not_7_out, A2_XOR_B2_out);
  and XOR3 (XOR3_out, not_6_out, XOR_A4_B4_A3_B3_out);
  not A1_prime (A1_prime_out, half_adder_4_sum);
  and A2_prime_B2 (A2_prime_B2_out, half_adder_9_sum, A1_prime_out);
  not not_8 (not_8_out, half_adder_10_sum);
  not not_9 (not_9_out, A1_XOR_B1_out);
  xor A1_XOR_B1 (A1_XOR_B1_out, half_adder_5_sum, half_adder_10_sum);
  or OR3 (OR3_out, OR2_out, and_7_out);
  and and_7 (and_7_out, A2_prime_B2_out, XOR3_out);
  or or_4 (out_13, or_3_out, and_10_out);
  and B1_prime_A1 (B1_prime_A1_out, half_adder_5_sum, not_8_out);
  and and_8 (out_15, not_9_out, not_4_out, not_2_out, not_6_out, not_7_out);
  and and_9 (and_9_out, and_6_out, not_7_out);
  and and_10 (and_10_out, and_9_out, B1_prime_A1_out);
  or or_5 (out_16, OR3_out, and_11_out);
  not not_10 (not_10_out, half_adder_5_sum);
  and XOR4 (XOR4_out, not_7_out, XOR3_out);
  and A1_prime_B1 (A1_prime_B1_out, not_10_out, half_adder_10_sum);
  and and_11 (and_11_out, A1_prime_B1_out, XOR4_out);
endmodule
